# Fritzing sketch light (saved by Fritzing 0.9.2b)
breadboards: 1

parts:
  Raspberry_Pi_1 = Raspberry Pi 3 [part_number=RPI-3-V1.2]
  LED1 = smd LED [color="Red (633nm)" package="0805 [SMD]"]
  R1 = PHOTOCELL [package=photocell-kit]
  C1 = Electrolytic Capacitor [capacitance=1µF package="100 mil [THT, electrolytic]"]

nets:
  3V3: Raspberry_Pi_1.3v3, Raspberry_Pi_1.3V3, R1.P$2
  N1: Raspberry_Pi_1.GIPO4, R1.P$1, C1.+
  N2: Raspberry_Pi_1.GIPO14, LED1.anode
  N3: Raspberry_Pi_1.GND, LED1.cathode, C1.-
