# Fritzing sketch push (saved by Fritzing 0.9.2b)
breadboards: 1

parts:
  Raspberry_Pi_1 = Raspberry Pi 3 [part_number=RPI-3-V1.2]
  LED1 = smd LED [color="Red (633nm)" package="0805 [SMD]"]
  S1 = Pushbutton [package="[SMD]"]
  R1 = Resistor [tolerance=±5% resistance=220 package=THT]
  R3 = Resistor [tolerance=±5% resistance=1k package="0805 [SMD]"]

nets:
  N1: Raspberry_Pi_1.GIPO23, S1.Pin_1, S1.Pin_2
  N2: Raspberry_Pi_1.GIPO14, LED1.anode
  N3: Raspberry_Pi_1.GND, R1.Pin_0, R3.Pin_0
  N4: LED1.cathode, R1.Pin_1
  N5: S1.Pin_3, S1.Pin_4, R3.Pin_1
